# Fritzing sketch day11-with-ky015 (saved by Fritzing 1.0.6)
breadboards: 2

parts:
  Mod1 = Raspberry Pi Pico
  OLED_128x32 = OLED 0.91" 128x32 I2C SSD1306 (GND/VCC)
  Button = Pushbutton [package="[THT]"]
  KY015 = KY-015 Temperature & Humidity Sensor Module [package="Breakout board"]
  Photo_resistor = LTR-301 [package=ltr-301]
  R1 = Resistor [tolerance=±5% power=0.25W resistance=10k package=THT]

nets:
  N1: Mod1.pin_1, OLED_128x32.SCA
  N2: Mod1.pin_2, OLED_128x32.SCL
  N3: Mod1.pin_3, Mod1.pin_8, Mod1.pin_13, Mod1.pin_18, Mod1.pin_23, Mod1.pin_28, Mod1.pin_33, Mod1.pin_38, Mod1.pin_42, OLED_128x32.GND, Photo_resistor.C, R1.Pin_1
  N4: Mod1.pin_11, Button.Pin_3, Button.Pin_4
  N5: Mod1.pin_31, KY015.S
  N6: Mod1.pin_32, KY015.-
  VCC: Mod1.pin_36, OLED_128x32.VCC, Button.Pin_1, Button.Pin_2, KY015.Vin, Photo_resistor.E

custom parts:
  Raspberry Pi Pico: Raspberry Pi Pico. Based around the RP2040 microcontroller the Pico is a low cost microcontroller device bringing Raspberry Pi quality, cost, and easy of use to the microcontroller space. Jan 2021, Split part in to two versions: tht (this one) and SMD. This one will drill holes for a .1 in header in pcb to allow plugging in the module as well as providing pads to solder the module to the top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
  OLED 0.91" 128x32 I2C SSD1306 (GND/VCC): OLED 0.91" 128x32 I2C SSD1306 Pinout: GND/VCC/SCL/SDA
  KY-015 Temperature & Humidity Sensor Module: KY-015 temperature and humidity sensor module, provides a low-latency serial interface to measure humidity and temperature.
