# Fritzing sketch day12-with-screen (saved by Fritzing 1.0.6)
breadboards: 2

parts:
  Mod1 = Raspberry Pi Pico
  OLED_128x32 = OLED 0.91" 128x32 I2C SSD1306 (GND/VCC)
  Button = Pushbutton [package="[THT]"]
  Potentiometer = Trimmer Potentiometer [maximum_resistance=10kΩ knob_status=50% power=0.5W package=THT]
  WS2812_(x15)_RGB_LED_strip = WS2812 RGB LED strip

nets:
  N1: Mod1.pin_1, OLED_128x32.SCA
  N2: Mod1.pin_2, OLED_128x32.SCL
  N3: Mod1.pin_3, Mod1.pin_8, Mod1.pin_13, Mod1.pin_18, Mod1.pin_23, Mod1.pin_28, Mod1.pin_33, Mod1.pin_38, Potentiometer.leg1, WS2812_(x15)_RGB_LED_strip.GND
  N4: Mod1.pin_11, Button.Pin_3, Button.Pin_4
  N5: Mod1.pin_31, Potentiometer.wiper
  N6: Mod1.pin_34, WS2812_(x15)_RGB_LED_strip.DIN
  N7: Mod1.pin_36, OLED_128x32.VCC, Button.Pin_1, Button.Pin_2, Potentiometer.leg2
  N8: Mod1.pin_40, WS2812_(x15)_RGB_LED_strip.VCC

custom parts:
  Raspberry Pi Pico: Raspberry Pi Pico. Based around the RP2040 microcontroller the Pico is a low cost microcontroller device bringing Raspberry Pi quality, cost, and easy of use to the microcontroller space. Jan 2021, Split part in to two versions: tht (this one) and SMD. This one will drill holes for a .1 in header in pcb to allow plugging in the module as well as providing pads to solder the module to the top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
  OLED 0.91" 128x32 I2C SSD1306 (GND/VCC): OLED 0.91" 128x32 I2C SSD1306 Pinout: GND/VCC/SCL/SDA
  WS2812 RGB LED strip: WS2812 strip
