# Fritzing sketch day7-alarm-with-buttons (saved by Fritzing 1.0.6)
circuit board: 8.46667cm x 5.64444cm
breadboards: 3

parts:
  BTN1_GP3 = Momentary Switch [package=ksa_sealed_tac_switch]
  BTN2_GP8 = Momentary Switch [package=ksa_sealed_tac_switch]
  BTN3_GP12 = Momentary Switch [package=ksa_sealed_tac_switch]
  Buzzer_GP17 = Piezo Speaker
  RED_LED = LED - 3mm [color="Red (633nm)" current=0.030A package="3 mm [THT]"]
  AMBER_LED = LED - 3mm [color="Yellow (592nm)" current=0.030A package="3 mm [THT]"]
  GREEN_LED = LED - 3mm [color="Green (555nm)" current=0.030A package="3 mm [THT]"]
  330_ohm = Resistor [tolerance=±5% power=0.25W resistance=330 package=THT]
  330_ohm1 = Resistor [tolerance=±5% power=0.25W resistance=330 package=THT]
  330_ohm2 = Resistor [tolerance=±5% power=0.25W resistance=330 package=THT]
  POT_10k = 6mm Trimmer Potentiometer [maximum_resistance=10kΩ knob_status=50% power=0.5W package=THT]
  Raspberry_Pico_H = Raspberry Pi Pico
  PIR1 = PIR sensor

nets:
  N1: BTN1_GP3.2, BTN2_GP8.2, BTN3_GP12.2, POT_10k.leg2, Raspberry_Pico_H.pin_36, PIR1.VDD
  N2: BTN1_GP3.4, Raspberry_Pico_H.pin_5
  N3: BTN2_GP8.4, Raspberry_Pico_H.pin_11
  N4: BTN3_GP12.4, Raspberry_Pico_H.pin_16
  N5: Buzzer_GP17.pin1, 330_ohm.Pin_0, 330_ohm1.Pin_0, 330_ohm2.Pin_0, POT_10k.leg1, Raspberry_Pico_H.pin_3, Raspberry_Pico_H.pin_8, Raspberry_Pico_H.pin_13, Raspberry_Pico_H.pin_18, Raspberry_Pico_H.pin_23, Raspberry_Pico_H.pin_28, Raspberry_Pico_H.pin_33, Raspberry_Pico_H.pin_38, Raspberry_Pico_H.pin_42, PIR1.GND
  N6: Buzzer_GP17.pin2, Raspberry_Pico_H.pin_17
  N7: RED_LED.cathode, 330_ohm.Pin_1
  N8: RED_LED.anode, Raspberry_Pico_H.pin_24
  N9: AMBER_LED.cathode, 330_ohm1.Pin_1
  N10: AMBER_LED.anode, Raspberry_Pico_H.pin_25
  N11: GREEN_LED.cathode, 330_ohm2.Pin_1
  N12: GREEN_LED.anode, Raspberry_Pico_H.pin_26
  N13: POT_10k.wiper, Raspberry_Pico_H.pin_31
  N14: Raspberry_Pico_H.pin_32, PIR1.SIG

custom parts:
  Raspberry Pi Pico: Raspberry Pi Pico. Based around the RP2040 microcontroller the Pico is a low cost microcontroller device bringing Raspberry Pi quality, cost, and easy of use to the microcontroller space. Jan 2021, Split part in to two versions: tht (this one) and SMD. This one will drill holes for a .1 in header in pcb to allow plugging in the module as well as providing pads to solder the module to the top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
